// Logisim project ALU_8_Bit.circ as structural Verilog: 3 circuits, main circuit main
module main (
  input  D,
  input  CLK,
  input  Load,
  input  D1,
  input  CLK1,
  output Q,
  output not_Q,
  output Q1,
  output not_Q1
);

  D_Flipflop d_flipflop_1 (.D(D), .CLK(CLK), .Q(Q), .not_Q(not_Q));
  Register_1_Bit register_1_bit_1 (.Load(Load), .D(D1), .CLK(CLK1), .Q(Q1), .Q_negiert(not_Q1));
endmodule

module D_Flipflop (
  input  D,
  input  CLK,
  output Q,
  output not_Q
);

  wire nand_1_out, nand_2_out, nand_3_out, nand_4_out, nand_5_out, nand_6_out, not_1_out, not_2_out,
       not_3_out;

  not not_1 (not_1_out, CLK);
  not not_2 (not_2_out, D);
  not not_3 (not_3_out, CLK);
  nand nand_1 (nand_1_out, D, not_1_out);
  nand nand_2 (nand_2_out, not_2_out, not_3_out);
  nand nand_3 (nand_3_out, nand_1_out, nand_4_out);
  nand nand_4 (nand_4_out, nand_3_out, nand_2_out);
  nand nand_5 (nand_5_out, nand_3_out, CLK);
  nand nand_6 (nand_6_out, CLK, nand_4_out);
  nand nand_7 (Q, nand_5_out, not_Q);
  nand nand_8 (not_Q, Q, nand_6_out);

  // Notes on the sheet:
  //   M1
  //   M2
  //   Master_Q
  //   Master_Q_negiert
  //   S1
  //   S2
  //   Slave_Q
  //   Slave_Q_negiert
endmodule

module Register_1_Bit (
  input  Load,
  input  D,
  input  CLK,
  output Q,
  output Q_negiert
);

  wire and_1_out, and_2_out, not_1_out, not_2_out, or_1_out;

  not not_1 (not_1_out, Load);
  not not_2 (not_2_out, not_1_out);
  and and_1 (and_1_out, Q, not_1_out);
  and and_2 (and_2_out, D, not_2_out);
  or or_1 (or_1_out, and_1_out, and_2_out);
  D_Flipflop d_flipflop_1 (.D(or_1_out), .CLK(CLK), .Q(Q), .not_Q(Q_negiert));

  // Notes on the sheet:
  //   D_2
  //   D_1
  //   D_fuer_Flipflop
endmodule
